# Fritzing sketch ESP32_radio (saved by Fritzing 0.9.3b)
circuit board: 8cm x 6cm
breadboards: 1

parts:
  SP2 = SPEAKER [package=pcb_mount_speaker]
  VS1053B2 = VS1053B
  AMP1 = GF1002 Stereo Amplifier
  M1 = DOIT Esp32 DevKit v1 (30 pins long, 11 pins width) [part_number=ESP32S-PIN30]
  TFT1 = Color 320x240 TFT Display, ILI9341 Controller Chip
  R1 = Trimmer Potentiometer [maximum_resistance=10kΩ package=THT]
  C1 = Ceramic Capacitor [capacitance=100nF package="100 mil [THT, multilayer]"]
  C2 = Ceramic Capacitor [capacitance=100nF package="100 mil [THT, multilayer]"]
  RE1 = Rotary Encoder [package=THT]
  S1 = Pushbutton [package=THT]
  C3 = Ceramic Capacitor [capacitance=100nF package="100 mil [THT, multilayer]"]
  J_ENC = male pin header, 5 pins [form="♂ (male)"]
  R6 = Resistor [tolerance=±5% resistance=1k package="0805 [SMD]"]
  R3 = Resistor [tolerance=±5% resistance=10k package="0805 [SMD]"]
  R2 = Resistor [tolerance=±5% resistance=10k package="0805 [SMD]"]
  R8 = Resistor [tolerance=±5% resistance=10k package="0805 [SMD]"]
  R7 = Resistor [tolerance=±5% resistance=10k package="0805 [SMD]"]
  U1 = Transformer [part_number=600:600 package=transformer]
  J_AUD_IN = male pin header, 3 pins [form="♂ (male)"]
  R9 = Resistor [tolerance=±5% resistance=1k package=THT]
  R10 = Resistor [tolerance=±5% resistance=1k package=THT]
  J_AUD_OUT = male pin header, 2 pins [form="♂ (male)"]

nets:
  N1: SP2.+, AMP1.LOUT-
  N2: SP2.-, AMP1.LOUT+
  3.3V: VS1053B2.Vcc, M1.3V3, TFT1.VCC, R1.leg2, J_ENC.pin5, R8.Pin_0, R7.Pin_0
  GND: VS1053B2.Gnd, M1.GND, TFT1.GND, C1.0, C2.0, RE1.EncoderPinC, S1.leg0, C3.0, J_ENC.pin1
  N3: VS1053B2.XCS, M1.D32
  N4: VS1053B2.XDCS, M1.D33, TFT1.D/C
  N5: VS1053B2.DREQ, M1.D35
  N6: VS1053B2.MOSI, M1.D23, TFT1.SDI_(MOSI)
  N7: VS1053B2.SCK, M1.D18, TFT1.SCK
  N8: VS1053B2.MISO, M1.D19, TFT1.SDO_(MISO)
  N9: VS1053B2.XRST, M1.EN, TFT1.Reset
  N10: AMP1.INPUTL, U1.4, J_AUD_OUT.pin2
  N11: AMP1.INPUTG, U1.3, J_AUD_OUT.pin1
  GPIO15: M1.D15, C3.1, R6.Pin_0
  GPIO2: M1.D2, C1.1, R3.Pin_1
  GPIO4: M1.D4, C2.1, R2.Pin_0
  N12: M1.D27, TFT1.CS
  N13: TFT1.LED, R1.wiper
  N14: RE1.EncoderPinA, J_ENC.pin3, R3.Pin_0, R8.Pin_1
  N15: RE1.EncoderPinB, J_ENC.pin4, R2.Pin_1, R7.Pin_1
  N16: S1.leg1, J_ENC.pin2, R6.Pin_1
  N17: U1.1, R9.Pin_1, R10.Pin_1
  N18: U1.2, J_AUD_IN.pin1
  N19: J_AUD_IN.pin2, R10.Pin_0
  N20: J_AUD_IN.pin3, R9.Pin_0

custom parts:
  VS1053B: VS1053B module
  GF1002 Stereo Amplifier: GF1002 6 Watt Stereo Amplifier
  DOIT Esp32 DevKit v1 (30 pins long, 11 pins width): The DOIT Esp32 DevKit v1 is one of the development board created by DOIT to evaluate the ESP-WROOM-32 module. It is based on the ESP32 microcontroller that boasts Wifi, Bluetooth, Ethernet and Low Power support all in a single chip. (vanepp) made breadboard work, adjusted pin numbering and labels and reduced size of schematic and cleaned up pcb. This chip is 30pins long (2 x15) and 11 pins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
  Color 320x240 TFT Display, ILI9341 Controller Chip: 2.2" TFT Display with ILI9341 Controller
